# Fritzing sketch healthcoin.fritzing (saved by Fritzing 0.9.3b)
breadboards: 1

parts:
  Part1 = Arduino Mega 2560 (Rev3)
  U1 = ESP32S-HiLetgo [part_number=ESP32S-HiLetgo]
  BAT2 = Battery Holders [package=battery-aa-kit]
  BAT1 = BATTERY-2 [package=battery-aa]
  Part2 = Logic Level Converter
  LCD1 = LCD screen
  Part3 = InvenSense MPU6050
  R1 = Rotary Potentiometer (Small) [maximum_resistance=100kΩ package=THT]
  R2 = Resistor [tolerance=±5% resistance=100 package=THT]

nets:
  N1: Part1.D19/RX1, U1.GPIO1
  N2: Part1.D18/TX1, Part2.TX_HV
  N3: Part1.SCL, Part3.SCL
  N4: Part1.SDA, Part3.SDA
  N5: Part1.D12_PWM, LCD1.RS
  N6: Part1.D11_PWM, LCD1.R/W
  N7: Part1.D2_PWM, LCD1.DB7
  N8: Part1.D3_PWM, LCD1.DB6
  N9: Part1.D4_PWM, LCD1.DB5
  N10: Part1.D5_PWM, LCD1.DB4
  GND: U1.GND, BAT1.-1, Part2.GND, LCD1.VSS, LCD1.LED-, Part3.GND, R1.leg2
  VIN: U1.VIN, BAT2.+, LCD1.VDD, Part3.VCC, R1.leg1, R2.Pin_0
  N11: U1.GPIO3, Part2.TX_LV
  N12: BAT2.-, BAT1.+1
  N13: LCD1.V0, R1.wiper
  N14: LCD1.LED+, R2.Pin_1

custom parts:
  ESP32S-HiLetgo: HiLetgo ESP-WROOM-32 ESP32 ESP-32S Development Board 2.4GHz Dual-Mode WiFi + Bluetooth Dual Cores Microcontroller The ESP32 integrated with Antenna switches, RF Balun, power amplifiers, low-noise amplifiers, filters, and management modules, and the entire solution occupies the least area of PCB. 2.4 GHz Wi-Fi plus Bluetooth dual-mode chip, with TSMC Ultra-low power consumption 40nm technology,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
